# Fritzing sketch BLEMeteoSketch (saved by Fritzing 0.9.3b)
breadboards: 1

parts:
  Arduino_Uno = Arduino Uno (Rev3)
  BMP280 = Adafruit_BMP280
  HM-10 = Bluetooth HM-10
  R1 = Resistor [tolerance=±5% resistance=1k package=THT]
  R2 = Resistor [tolerance=±5% resistance=2k package=THT]
  MQ-135 = Gas Sensor Breakout Board
  AM_2302 = AM2302 Humidity and Temperature Sensor

nets:
  N1: Arduino_Uno.A0, MQ-135.AOUT
  N2: Arduino_Uno.A4/SDA, BMP280.SDI/SDA
  N3: Arduino_Uno.A5/SCL, BMP280.SCK/SCL
  N4: Arduino_Uno.D8, HM-10.TXD
  N5: Arduino_Uno.D9_PWM, R1.Pin_1
  N6: Arduino_Uno.D2, AM_2302.DATA
  3V3: Arduino_Uno.3V3, BMP280.3.3V
  5V: Arduino_Uno.5V, HM-10.VCC, MQ-135.5V, AM_2302.VDD
  GND: Arduino_Uno.GND, BMP280.GND, HM-10.GND, R2.Pin_1, MQ-135.GND, AM_2302.GND
  N7: HM-10.RXD, R1.Pin_0, R2.Pin_0

custom parts:
  Adafruit_BMP280: Bosch has stepped up their game with their new BMP280 sensor, an environmental sensor with temperature, barometric pressure that is the next generation upgrade to the BMP085/BMP180/BMP183. This sensor is great for all sorts of weather sensing and can even be used in both I2C and SPI! This precision sensor from Bosch is the best low-cost, precision sensing solution for measuring barometric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
  Gas Sensor Breakout Board: Gas sensor breakout board. Input voltage is 5V. Sensor output is available in analog and digital.
